// Logisim project CPUArch.circ as structural Verilog: 4 circuits, main circuit main
module main (
);

  Memory memory_1 ();  // open: Op, Clk, Q
endmodule

module ALU (
  input  [7:0] D,
  input  Op,
  output [7:0] Q
);

  wire [7:0] adder_1_out, subtractor_1_out;

  Adder adder_1 (.a(D), .b({8{1'b0}}), .out(adder_1_out), .cin(1'b1));  // open: cout
  Subtractor subtractor_1 (.a(D), .b({8{1'b0}}), .out(subtractor_1_out), .bin(1'b1));  // open: bout
  Multiplexer #(.width(8)) multiplexer_1 (.in0(adder_1_out), .in1(subtractor_1_out), .out(Q), .sel(Op));
endmodule

module Memory (
  input  [1:0] Op,
  input  Clk,
  output [7:0] Q
);

  wire not_1_out, not_2_out;
  wire [7:0] alu_1_q, counter_1_q;

  not not_1 (not_1_out, Op[0]);
  Counter counter_1 (.up(not_1_out), .count(Op[1]), .clk(Clk), .Q(counter_1_q));  // open: clr, load, D, carry
  ALU alu_1 (.D(Q), .Op(Op[0]), .Q(alu_1_q));
  RAM ram_1 (.addr(counter_1_q), .we(not_2_out), .oe(1'b1), .clk(Clk), .din(alu_1_q), .dout(Q));
  not not_2 (not_2_out, Op[1]);
endmodule

module Program (
  output [2:0] out_1
);

  wire [3:0] rom_1_data;
  wire [7:0] counter_1_q;

  ROM #(.dataWidth(4)) rom_1 (.addr(counter_1_q), .data(rom_1_data));
  Counter counter_1 (.Q(counter_1_q));  // open: load, D, count, carry, up, clk, clr
  PLA #(.in_width(4), .out_width(3), .\table ("0001 000 # +\n0010 000 # -\n0011 000 # <\n0100 000 # >\n0101 000 # ,\n0110 000 # .\n0111 000 # @\n1000 000 # !\n1111 000 # HALT")) pla_1 (
    .in(rom_1_data), .out(out_1));
endmodule
